// Logisim project ex6.circ as structural Verilog: 1 circuit, main circuit main
module main (
  input  in_1,
  input  in_2,
  input  in_3,
  output Out_6,
  output Out_5,
  output Out_4,
  output Out_3,
  output Out_2,
  output Out_1,
  output Out_0
);

  wire and_3_out, and_4_out, and_5_out;

  and and_1 (Out_6, in_1, in_2, in_3);
  and and_2 (Out_5, in_1, in_2);
  and and_3 (and_3_out, in_1, in_2);
  and and_4 (and_4_out, in_1, in_3);
  and and_5 (and_5_out, in_2, in_3);
  or or_1 (Out_1, in_1, in_2);
  or or_2 (Out_0, in_1, in_2, in_3);
  or or_3 (Out_4, and_3_out, and_4_out);
  or or_4 (Out_2, in_1, and_5_out);

  assign Out_3 = in_1;

  // Notes on the sheet:
  //   In_2
  //   In_1
  //   In_0
endmodule
